// Logisim project mips-cpu.circ as structural Verilog
module MIPS_CPU (
);

  wire clock_1_out;
  wire [31:0] adder_1_out, alu_1_result, data_memory_1_read_data, instr_memory_1_instruction, PC_q,
       reg_file_1_read_data_1, reg_file_1_read_data_2;

  Clock clock_1 (.out(clock_1_out));
  Register #(.width(32)) PC (.D(adder_1_out), .Q(PC_q), .clk(clock_1_out));  // open: en, clr
  Adder #(.width(32)) adder_1 (.a(32'h4), .b(PC_q), .out(adder_1_out));  // open: cin, cout
  Instr_Memory instr_memory_1 (.Read_Address(PC_q), .Instruction(instr_memory_1_instruction));
  Reg_File reg_file_1 (
    .Read_Reg_1(instr_memory_1_instruction[25:21]), .Write_Data(alu_1_result),
    .Write_Reg(instr_memory_1_instruction[15:11]), .Read_Reg_2(instr_memory_1_instruction[20:16]),
    .Read_Data_1(reg_file_1_read_data_1), .Read_Data_2(reg_file_1_read_data_2));
  ALU alu_1 (
    .A(reg_file_1_read_data_1), .B(reg_file_1_read_data_2), .Result(alu_1_result));  // open: ALU_Control, out_5
  Data_Memory data_memory_1 (
    .Address(alu_1_result), .Write_Data(reg_file_1_read_data_2), .Read_Data(data_memory_1_read_data));

  // Notes on the sheet:
  //   op
  //   rs
  //   rt
  //   rd
endmodule

module ALU (
  input  [31:0] A,
  input  [31:0] B,
  input  [3:0] ALU_Control,
  output [31:0] Result,
  output out_5
);

  wire [31:0] adder_1_out, and_1_out, or_1_out, subtractor_1_out;

  Adder #(.width(32)) adder_1 (.a(A), .b(B), .out(adder_1_out));  // open: cin, cout
  assign and_1_out = A & B;  // AND_Gate and_1, 32 bits wide
  assign or_1_out = A | B;  // OR_Gate or_1, 32 bits wide
  Subtractor #(.width(32)) subtractor_1 (.a(A), .b(B), .out(subtractor_1_out));  // open: bin, bout
  Multiplexer #(.select(4), .width(32), .enable("false")) multiplexer_1 (
    .in0(adder_1_out), .in1(and_1_out), .in2(or_1_out), .in3(subtractor_1_out), .out(Result),
    .sel(ALU_Control));  // open: in4, in5, in6, in7, in8, in9, in10, in11, in12, in13, in14, in15
endmodule

module Reg_File (
  input  [4:0] Read_Reg_1,
  input  [31:0] Write_Data,
  input  [4:0] Write_Reg,
  input  [4:0] Read_Reg_2,
  output [31:0] Read_Data_1,
  output [31:0] Read_Data_2
);

  wire [31:0] demultiplexer_1_out0, demultiplexer_1_out1, demultiplexer_1_out2, demultiplexer_1_out3,
       demultiplexer_1_out4, demultiplexer_1_out5, demultiplexer_1_out6, demultiplexer_1_out7,
       demultiplexer_1_out8, demultiplexer_1_out9, demultiplexer_1_out10, demultiplexer_1_out11,
       demultiplexer_1_out12, demultiplexer_1_out13, demultiplexer_1_out14, demultiplexer_1_out15,
       demultiplexer_1_out16, demultiplexer_1_out17, demultiplexer_1_out18, demultiplexer_1_out19,
       demultiplexer_1_out20, demultiplexer_1_out21, demultiplexer_1_out22, demultiplexer_1_out23,
       demultiplexer_1_out24, demultiplexer_1_out25, demultiplexer_1_out26, demultiplexer_1_out27,
       demultiplexer_1_out28, demultiplexer_1_out29, demultiplexer_1_out30, demultiplexer_1_out31,
       register_1_q, register_2_q, register_3_q, register_4_q, register_5_q, register_6_q, register_7_q,
       register_8_q, register_9_q, register_10_q, register_11_q, register_12_q, register_13_q, register_14_q,
       register_15_q, register_16_q, register_17_q, register_18_q, register_19_q, register_20_q,
       register_21_q, register_22_q, register_23_q, register_24_q, register_25_q, register_26_q,
       register_27_q, register_28_q, register_29_q, register_30_q, register_31_q, register_32_q;

  Demultiplexer #(.select(5), .width(32), .enable("false")) demultiplexer_1 (
    .out0(demultiplexer_1_out0), .out1(demultiplexer_1_out1), .out2(demultiplexer_1_out2),
    .out3(demultiplexer_1_out3), .out4(demultiplexer_1_out4), .out5(demultiplexer_1_out5),
    .out6(demultiplexer_1_out6), .out7(demultiplexer_1_out7), .out8(demultiplexer_1_out8),
    .out9(demultiplexer_1_out9), .out10(demultiplexer_1_out10), .out11(demultiplexer_1_out11),
    .out12(demultiplexer_1_out12), .out13(demultiplexer_1_out13), .out14(demultiplexer_1_out14),
    .out15(demultiplexer_1_out15), .out16(demultiplexer_1_out16), .out17(demultiplexer_1_out17),
    .out18(demultiplexer_1_out18), .out19(demultiplexer_1_out19), .out20(demultiplexer_1_out20),
    .out21(demultiplexer_1_out21), .out22(demultiplexer_1_out22), .out23(demultiplexer_1_out23),
    .out24(demultiplexer_1_out24), .out25(demultiplexer_1_out25), .out26(demultiplexer_1_out26),
    .out27(demultiplexer_1_out27), .out28(demultiplexer_1_out28), .out29(demultiplexer_1_out29),
    .out30(demultiplexer_1_out30), .out31(demultiplexer_1_out31), .in(Write_Data), .sel(Write_Reg));
  Register #(.width(32)) register_1 (.D(demultiplexer_1_out0), .Q(register_1_q));  // open: en, clk, clr
  Register #(.width(32)) register_2 (.D(demultiplexer_1_out4), .Q(register_2_q));  // open: en, clk, clr
  Register #(.width(32)) register_3 (.D(demultiplexer_1_out8), .Q(register_3_q));  // open: en, clk, clr
  Register #(.width(32)) register_4 (.D(demultiplexer_1_out12), .Q(register_4_q));  // open: en, clk, clr
  Register #(.width(32)) register_5 (.D(demultiplexer_1_out16), .Q(register_5_q));  // open: en, clk, clr
  Register #(.width(32)) register_6 (.D(demultiplexer_1_out20), .Q(register_6_q));  // open: en, clk, clr
  Register #(.width(32)) register_7 (.D(demultiplexer_1_out24), .Q(register_7_q));  // open: en, clk, clr
  Register #(.width(32)) register_8 (.D(demultiplexer_1_out28), .Q(register_8_q));  // open: en, clk, clr
  Register #(.width(32)) register_9 (.D(demultiplexer_1_out1), .Q(register_9_q));  // open: en, clk, clr
  Register #(.width(32)) register_10 (.D(demultiplexer_1_out5), .Q(register_10_q));  // open: en, clk, clr
  Register #(.width(32)) register_11 (.D(demultiplexer_1_out9), .Q(register_11_q));  // open: en, clk, clr
  Register #(.width(32)) register_12 (.D(demultiplexer_1_out13), .Q(register_12_q));  // open: en, clk, clr
  Register #(.width(32)) register_13 (.D(demultiplexer_1_out17), .Q(register_13_q));  // open: en, clk, clr
  Register #(.width(32)) register_14 (.D(demultiplexer_1_out21), .Q(register_14_q));  // open: en, clk, clr
  Register #(.width(32)) register_15 (.D(demultiplexer_1_out25), .Q(register_15_q));  // open: en, clk, clr
  Register #(.width(32)) register_16 (.D(demultiplexer_1_out29), .Q(register_16_q));  // open: en, clk, clr
  Register #(.width(32)) register_17 (.D(demultiplexer_1_out2), .Q(register_17_q));  // open: en, clk, clr
  Register #(.width(32)) register_18 (.D(demultiplexer_1_out6), .Q(register_18_q));  // open: en, clk, clr
  Register #(.width(32)) register_19 (.D(demultiplexer_1_out10), .Q(register_19_q));  // open: en, clk, clr
  Register #(.width(32)) register_20 (.D(demultiplexer_1_out14), .Q(register_20_q));  // open: en, clk, clr
  Register #(.width(32)) register_21 (.D(demultiplexer_1_out18), .Q(register_21_q));  // open: en, clk, clr
  Register #(.width(32)) register_22 (.D(demultiplexer_1_out22), .Q(register_22_q));  // open: en, clk, clr
  Register #(.width(32)) register_23 (.D(demultiplexer_1_out26), .Q(register_23_q));  // open: en, clk, clr
  Register #(.width(32)) register_24 (.D(demultiplexer_1_out30), .Q(register_24_q));  // open: en, clk, clr
  Register #(.width(32)) register_25 (.D(demultiplexer_1_out3), .Q(register_25_q));  // open: en, clk, clr
  Register #(.width(32)) register_26 (.D(demultiplexer_1_out7), .Q(register_26_q));  // open: en, clk, clr
  Register #(.width(32)) register_27 (.D(demultiplexer_1_out11), .Q(register_27_q));  // open: en, clk, clr
  Register #(.width(32)) register_28 (.D(demultiplexer_1_out15), .Q(register_28_q));  // open: en, clk, clr
  Register #(.width(32)) register_29 (.D(demultiplexer_1_out19), .Q(register_29_q));  // open: en, clk, clr
  Register #(.width(32)) register_30 (.D(demultiplexer_1_out23), .Q(register_30_q));  // open: en, clk, clr
  Register #(.width(32)) register_31 (.D(demultiplexer_1_out27), .Q(register_31_q));  // open: en, clk, clr
  Register #(.width(32)) register_32 (.D(demultiplexer_1_out31), .Q(register_32_q));  // open: en, clk, clr
  Multiplexer #(.select(5), .width(32), .enable("false")) multiplexer_1 (
    .in0(register_1_q), .in1(register_9_q), .in2(register_17_q), .in3(register_25_q), .in4(register_2_q),
    .in5(register_10_q), .in6(register_18_q), .in7(register_26_q), .in8(register_3_q), .in9(register_11_q),
    .in10(register_19_q), .in11(register_27_q), .in12(register_4_q), .in13(register_12_q),
    .in14(register_20_q), .in15(register_28_q), .in16(register_5_q), .in17(register_13_q),
    .in18(register_21_q), .in19(register_29_q), .in20(register_6_q), .in21(register_14_q),
    .in22(register_22_q), .in23(register_30_q), .in24(register_7_q), .in25(register_15_q),
    .in26(register_23_q), .in27(register_31_q), .in28(register_8_q), .in29(register_16_q),
    .in30(register_24_q), .in31(register_32_q), .out(Read_Data_1), .sel(Read_Reg_1));
  Multiplexer #(.select(5), .width(32), .enable("false")) multiplexer_2 (
    .in0(register_1_q), .in1(register_9_q), .in2(register_17_q), .in3(register_25_q), .in4(register_2_q),
    .in5(register_10_q), .in6(register_18_q), .in7(register_26_q), .in8(register_3_q), .in9(register_11_q),
    .in10(register_19_q), .in11(register_27_q), .in12(register_4_q), .in13(register_12_q),
    .in14(register_20_q), .in15(register_28_q), .in16(register_5_q), .in17(register_13_q),
    .in18(register_21_q), .in19(register_29_q), .in20(register_6_q), .in21(register_14_q),
    .in22(register_22_q), .in23(register_30_q), .in24(register_7_q), .in25(register_15_q),
    .in26(register_23_q), .in27(register_31_q), .in28(register_8_q), .in29(register_16_q),
    .in30(register_24_q), .in31(register_32_q), .out(Read_Data_2), .sel(Read_Reg_2));

  // Notes on the sheet:
  //   $zero
  //   $ra
endmodule

module Instr_Memory (
  input  [31:0] Read_Address,
  output [31:0] Instruction
);

  RAM #(.addrWidth(24), .dataWidth(32), .bus("separate")) ram_1 (
    .addr(Read_Address[23:0]), .data(Instruction));  // open: din, str, sel, clk, ld, clr
endmodule

module Data_Memory (
  input  [31:0] Address,
  input  [31:0] Write_Data,
  output [31:0] Read_Data
);

  RAM #(.addrWidth(24), .dataWidth(32), .bus("separate")) ram_1 (
    .addr(Address[23:0]), .din(Write_Data), .data(Read_Data));  // open: str, sel, clk, ld, clr
endmodule
